# Fritzing sketch irmanakaza (saved by Fritzing 0.8.7b)
breadboards: 1

parts:
  Part1 = Arduino Uno (Rev3)
  Part2 = Digital Temperature Sensor Breakout - TMP102
  LED1 = LED - 5mm [color="Red (633nm)" package="5 mm [THT]"]  # not connected

nets:
  GND: Part1.GND, Part2.GND
  N1: Part1.D7, Part2.SDA
  N2: Part1.5V, Part2.SCL
